// Logisim project y86.circ as structural Verilog: 26 circuits, main circuit main
module main (
  input  in_1,
  input  in_2
);

  wire clock_1_out, cond_1_cnd, memread_1_read, memwrite_1_write, needregids_1_need_regids,
       needvalc_1_need_valc, setcc_1_set;
  wire [1:0] alufunc_1_alufun;
  wire [2:0] alu_1_zso, cc_1_ccc;
  wire [3:0] align_1_ra, align_1_rb, cyclecount_1_cyclenum, dste_1_de, dstm_1_dm, new_pc_1_newpc,
       new_pc_1_newpc_2, new_pc_1_newpc_3, new_pc_1_newpc_4, new_pc_1_newpc_5, new_pc_1_newpc_6,
       new_pc_1_newpc_7, new_pc_1_newpc_8, new_pc_1_newpc_9, new_pc_1_newpc_10, new_pc_1_newpc_11,
       new_pc_1_newpc_12, new_pc_1_newpc_13, new_pc_1_newpc_14, new_pc_1_newpc_15, new_pc_1_newpc_16,
       srca_1_sa, srcb_1_sb;
  wire [7:0] instruction_memory_1_byte0, instruction_memory_1_byte1, instruction_memory_1_byte2,
       instruction_memory_1_byte3, instruction_memory_1_byte4, instruction_memory_1_byte5,
       instruction_memory_1_byte6, instruction_memory_1_byte7, instruction_memory_1_byte8,
       instruction_memory_1_byte9;
  wire [15:0] cyclecount_1_linenum;
  wire [63:0] align_1_valc, alu_1_vale, alua_1_out_4, alub_1_out_3, data_memory_1_valm, memaddress_1_addr,
       memdata_1_data, pcinc_1_valp, register_file_1_r8, register_file_1_r9, register_file_1_r10,
       register_file_1_r11, register_file_1_r12, register_file_1_r13, register_file_1_r14,
       register_file_1_rax, register_file_1_rbp, register_file_1_rbx, register_file_1_rcx,
       register_file_1_rdi, register_file_1_rdx, register_file_1_rsi, register_file_1_rsp,
       register_file_1_vala, register_file_1_valb;

  Clock clock_1 (.out(clock_1_out));
  // Probe on {new_pc_1_newpc_13, new_pc_1_newpc_12, new_pc_1_newpc_11, new_pc_1_newpc_10, new_pc_1_newpc_9, new_pc_1_newpc_8, new_pc_1_newpc_7, new_pc_1_newpc_6, new_pc_1_newpc_5, new_pc_1_newpc_4, new_pc_1_newpc_3, new_pc_1_newpc_2, new_pc_1_newpc, new_pc_1_newpc_16, new_pc_1_newpc_15, new_pc_1_newpc_14}
  Instruction_Memory instruction_memory_1 (
    .PC({new_pc_1_newpc_16, new_pc_1_newpc_15, new_pc_1_newpc_14}), .Clock(clock_1_out),
    .Byte0(instruction_memory_1_byte0), .Byte1(instruction_memory_1_byte1),
    .Byte2(instruction_memory_1_byte2), .Byte3(instruction_memory_1_byte3),
    .Byte4(instruction_memory_1_byte4), .Byte5(instruction_memory_1_byte5),
    .Byte6(instruction_memory_1_byte6), .Byte7(instruction_memory_1_byte7),
    .Byte8(instruction_memory_1_byte8), .Byte9(instruction_memory_1_byte9));
  // Probe on cyclecount_1_linenum
  CycleCount cyclecount_1 (
    .icode(instruction_memory_1_byte0[7:4]), .clock(clock_1_out), .LineNum(cyclecount_1_linenum),
    .CycleNum(cyclecount_1_cyclenum));
  // Probe on cyclecount_1_cyclenum
  // Probe on instruction_memory_1_byte0[7:4]
  // Probe on instruction_memory_1_byte0[3:0]
  // Probe on align_1_ra
  // Probe on align_1_rb
  NeedRegIDs needregids_1 (.icode(instruction_memory_1_byte0[7:4]), .Need_RegIDs(needregids_1_need_regids));
  NeedValC needvalc_1 (.icode(instruction_memory_1_byte0[7:4]), .Need_ValC(needvalc_1_need_valc));
  // Probe on align_1_valc
  // Probe on pcinc_1_valp
  Align align_1 (
    .Byte1(instruction_memory_1_byte1), .Byte2(instruction_memory_1_byte2),
    .Byte3(instruction_memory_1_byte3), .Byte4(instruction_memory_1_byte4),
    .Byte5(instruction_memory_1_byte5), .Byte6(instruction_memory_1_byte6),
    .Byte7(instruction_memory_1_byte7), .Byte8(instruction_memory_1_byte8),
    .Byte9(instruction_memory_1_byte9), .NeedRegIDs(needregids_1_need_regids), .rA(align_1_ra),
    .rB(align_1_rb), .valC(align_1_valc));
  PCinc pcinc_1 (
    .PC({new_pc_1_newpc_13, new_pc_1_newpc_12, new_pc_1_newpc_11, new_pc_1_newpc_10, new_pc_1_newpc_9, new_pc_1_newpc_8, new_pc_1_newpc_7, new_pc_1_newpc_6, new_pc_1_newpc_5, new_pc_1_newpc_4, new_pc_1_newpc_3, new_pc_1_newpc_2, new_pc_1_newpc, new_pc_1_newpc_16, new_pc_1_newpc_15, new_pc_1_newpc_14}),
    .NeedRegIDS(needregids_1_need_regids), .NeedValC(needvalc_1_need_valc), .valP(pcinc_1_valp));
  srcA srca_1 (.icode(instruction_memory_1_byte0[7:4]), .rA(align_1_ra), .sA(srca_1_sa));
  srcB srcb_1 (.icode(instruction_memory_1_byte0[7:4]), .rB(align_1_rb), .sB(srcb_1_sb));
  dstE dste_1 (.icode(instruction_memory_1_byte0[7:4]), .rB(align_1_rb), .dE(dste_1_de));
  dstM dstm_1 (.icode(instruction_memory_1_byte0[7:4]), .rA(align_1_ra), .dM(dstm_1_dm));
  // Probe on srca_1_sa
  // Probe on srcb_1_sb
  // Probe on dste_1_de
  // Probe on dstm_1_dm
  Register_File register_file_1 (
    .srcA(srca_1_sa), .srcB(srcb_1_sb), .valE(alu_1_vale), .valM(data_memory_1_valm), .dstE(dste_1_de),
    .dstM(dstm_1_dm), .in_7(in_1), .in_8(in_2), .clk(clock_1_out), .valA(register_file_1_vala),
    .valB(register_file_1_valb), .rax(register_file_1_rax), .rcx(register_file_1_rcx),
    .rdx(register_file_1_rdx), .rbx(register_file_1_rbx), .rsp(register_file_1_rsp),
    .rbp(register_file_1_rbp), .rsi(register_file_1_rsi), .rdi(register_file_1_rdi), .r8(register_file_1_r8),
    .r9(register_file_1_r9), .r10(register_file_1_r10), .r11(register_file_1_r11), .r12(register_file_1_r12),
    .r13(register_file_1_r13), .r14(register_file_1_r14));
  // Probe on register_file_1_rax
  // Probe on register_file_1_rcx
  // Probe on register_file_1_rdx
  // Probe on register_file_1_rbx
  // Probe on register_file_1_rsp
  // Probe on register_file_1_rbp
  // Probe on register_file_1_rsi
  // Probe on register_file_1_rdi
  // Probe on register_file_1_r8
  // Probe on register_file_1_r9
  // Probe on register_file_1_r10
  // Probe on register_file_1_r11
  // Probe on register_file_1_r12
  // Probe on register_file_1_r13
  // Probe on register_file_1_r14
  // Probe on register_file_1_vala
  // Probe on register_file_1_valb
  ALUA alua_1 (
    .valA(register_file_1_vala), .valC(align_1_valc), .icode(instruction_memory_1_byte0[7:4]),
    .out_4(alua_1_out_4));
  ALUB alub_1 (.valB(register_file_1_valb), .icode(instruction_memory_1_byte0[7:4]), .out_3(alub_1_out_3));
  ALUfunc alufunc_1 (
    .icode(instruction_memory_1_byte0[7:4]), .ifun(instruction_memory_1_byte0[3:0]), .alufun(alufunc_1_alufun));
  // Probe on alua_1_out_4
  // Probe on alub_1_out_3
  // Probe on alufunc_1_alufun
  SetCC setcc_1 (.icode(instruction_memory_1_byte0[7:4]), .set(setcc_1_set));
  ALU alu_1 (
    .ALUfunc(alufunc_1_alufun), .AluA(alua_1_out_4), .AluB(alub_1_out_3), .Clk(clock_1_out),
    .valE(alu_1_vale), .ZSO(alu_1_zso));
  // Probe on alu_1_vale
  // Probe on alu_1_zso
  // Probe on cc_1_ccc
  CC cc_1 (.ZSO(alu_1_zso), .setcc(setcc_1_set), .Clk(clock_1_out), .CCc(cc_1_ccc));
  MemAddress memaddress_1 (
    .valA(register_file_1_vala), .icode(instruction_memory_1_byte0[7:4]), .valE(alu_1_vale),
    .Addr(memaddress_1_addr));
  MemData memdata_1 (
    .valA(register_file_1_vala), .icode(instruction_memory_1_byte0[7:4]), .valP(pcinc_1_valp),
    .Data(memdata_1_data));
  MemRead memread_1 (.icode(instruction_memory_1_byte0[7:4]), .Read(memread_1_read));
  MemWrite memwrite_1 (.icode(instruction_memory_1_byte0[7:4]), .Write(memwrite_1_write));
  // Probe on memaddress_1_addr
  // Probe on memdata_1_data
  // Probe on memread_1_read
  // Probe on memwrite_1_write
  Cond cond_1 (.ifun(instruction_memory_1_byte0[3:0]), .CC(cc_1_ccc), .Cnd(cond_1_cnd));
  Data_Memory data_memory_1 (
    .Read(memread_1_read), .Write(memwrite_1_write), .Addr(memaddress_1_addr), .Data(memdata_1_data),
    .Clk(clock_1_out), .valM(data_memory_1_valm));
  // Probe on data_memory_1_valm
  New_PC new_pc_1 (
    .icode(instruction_memory_1_byte0[7:4]), .Cnd(cond_1_cnd), .valP(pcinc_1_valp), .valC(align_1_valc),
    .valM(data_memory_1_valm), .Clk(clock_1_out),
    .PC({new_pc_1_newpc_13, new_pc_1_newpc_12, new_pc_1_newpc_11, new_pc_1_newpc_10, new_pc_1_newpc_9, new_pc_1_newpc_8, new_pc_1_newpc_7, new_pc_1_newpc_6, new_pc_1_newpc_5, new_pc_1_newpc_4, new_pc_1_newpc_3, new_pc_1_newpc_2, new_pc_1_newpc, new_pc_1_newpc_16, new_pc_1_newpc_15, new_pc_1_newpc_14}),
    .NewPC({new_pc_1_newpc_13, new_pc_1_newpc_12, new_pc_1_newpc_11, new_pc_1_newpc_10, new_pc_1_newpc_9, new_pc_1_newpc_8, new_pc_1_newpc_7, new_pc_1_newpc_6, new_pc_1_newpc_5, new_pc_1_newpc_4, new_pc_1_newpc_3, new_pc_1_newpc_2, new_pc_1_newpc, new_pc_1_newpc_16, new_pc_1_newpc_15, new_pc_1_newpc_14}));

  // Notes on the sheet:
  //   ZSO = 
endmodule

module CycleCount (
  input  [3:0] icode,
  input  clock,
  output [15:0] LineNum,
  output [3:0] CycleNum
);

  wire and_1_out, and_2_out, and_3_out, not_1_out, not_2_out, not_3_out, not_4_out, not_5_out, not_6_out;

  not not_1 (not_1_out, icode[0]);
  not not_2 (not_2_out, icode[1]);
  not not_3 (not_3_out, icode[2]);
  not not_4 (not_4_out, icode[3]);
  Counter #(.max('hd), .width(4)) counter_1 (.Q(CycleNum), .clk(clock));  // open: load, D, count, carry, up, clr
  and and_1 (and_1_out, not_1_out, not_2_out, not_3_out, not_4_out);
  not not_5 (not_5_out, CycleNum[1]);
  and and_2 (and_2_out, CycleNum[0], not_5_out, CycleNum[2], CycleNum[3]);
  not not_6 (not_6_out, and_1_out);
  and and_3 (and_3_out, not_6_out, and_2_out);
  Counter #(.max('hffff), .width(16)) counter_2 (.Q(LineNum), .clk(and_3_out));  // open: load, D, count, carry, up, clr
endmodule

module Fetch (
  input  [63:0] PC,
  input  Clk,
  output [3:0] icode,
  output [3:0] ifun,
  output [3:0] rA,
  output [3:0] rB,
  output [63:0] valC,
  output [63:0] valP
);

  wire needregids_1_need_regids, needvalc_1_need_valc;
  wire [7:0] instruction_memory_1_byte1, instruction_memory_1_byte2, instruction_memory_1_byte3,
       instruction_memory_1_byte4, instruction_memory_1_byte5, instruction_memory_1_byte6,
       instruction_memory_1_byte7, instruction_memory_1_byte8, instruction_memory_1_byte9;

  Instruction_Memory instruction_memory_1 (
    .PC(PC[11:0]), .Clock(Clk), .Byte0({icode, ifun}), .Byte1(instruction_memory_1_byte1),
    .Byte2(instruction_memory_1_byte2), .Byte3(instruction_memory_1_byte3),
    .Byte4(instruction_memory_1_byte4), .Byte5(instruction_memory_1_byte5),
    .Byte6(instruction_memory_1_byte6), .Byte7(instruction_memory_1_byte7),
    .Byte8(instruction_memory_1_byte8), .Byte9(instruction_memory_1_byte9));
  NeedRegIDs needregids_1 (.icode(icode), .Need_RegIDs(needregids_1_need_regids));
  NeedValC needvalc_1 (.icode(icode), .Need_ValC(needvalc_1_need_valc));
  Align align_1 (
    .Byte1(instruction_memory_1_byte1), .Byte2(instruction_memory_1_byte2),
    .Byte3(instruction_memory_1_byte3), .Byte4(instruction_memory_1_byte4),
    .Byte5(instruction_memory_1_byte5), .Byte6(instruction_memory_1_byte6),
    .Byte7(instruction_memory_1_byte7), .Byte8(instruction_memory_1_byte8),
    .Byte9(instruction_memory_1_byte9), .NeedRegIDs(needregids_1_need_regids), .rA(rA), .rB(rB), .valC(valC));
  PCinc pcinc_1 (.PC(PC), .NeedRegIDS(needregids_1_need_regids), .NeedValC(needvalc_1_need_valc), .valP(valP));
endmodule

module Instruction_Memory (
  input  [11:0] PC,
  input  Clock,
  output [7:0] Byte0,
  output [7:0] Byte1,
  output [7:0] Byte2,
  output [7:0] Byte3,
  output [7:0] Byte4,
  output [7:0] Byte5,
  output [7:0] Byte6,
  output [7:0] Byte7,
  output [7:0] Byte8,
  output [7:0] Byte9
);

  wire decoder_1_out0, decoder_1_out1, decoder_1_out2, decoder_1_out3, decoder_1_out4, decoder_1_out5,
       decoder_1_out6, decoder_1_out7, decoder_1_out8, decoder_1_out9;
  wire [3:0] counter_2_q;
  wire [7:0] rom_1_data;
  wire [11:0] adder_1_out, counter_1_q;

  Counter #(.max('hd), .width(12)) counter_1 (.Q(counter_1_q), .clk(Clock));  // open: load, D, count, carry, up, clr
  Counter #(.max('hd), .width(4)) counter_2 (.Q(counter_2_q), .clk(Clock));  // open: load, D, count, carry, up, clr
  Decoder #(.enable("false"), .select(4)) decoder_1 (
    .out0(decoder_1_out0), .out1(decoder_1_out1), .out2(decoder_1_out2), .out3(decoder_1_out3),
    .out4(decoder_1_out4), .out5(decoder_1_out5), .out6(decoder_1_out6), .out7(decoder_1_out7),
    .out8(decoder_1_out8), .out9(decoder_1_out9), .sel(counter_2_q));  // open: out10, out11, out12, out13, out14, out15
  Adder #(.width(12)) adder_1 (.a(PC), .b(counter_1_q), .out(adder_1_out));  // open: cin, cout
  ROM #(.addrWidth(12)) rom_1 (.addr(adder_1_out), .data(rom_1_data));
  Register register_1 (.D(rom_1_data), .en(decoder_1_out0), .clk(Clock), .Q(Byte0));  // open: clr
  Register register_2 (.D(rom_1_data), .en(decoder_1_out1), .clk(Clock), .Q(Byte1));  // open: clr
  Register register_3 (.D(rom_1_data), .en(decoder_1_out2), .clk(Clock), .Q(Byte2));  // open: clr
  Register register_4 (.D(rom_1_data), .en(decoder_1_out3), .clk(Clock), .Q(Byte3));  // open: clr
  Register register_5 (.D(rom_1_data), .en(decoder_1_out4), .clk(Clock), .Q(Byte4));  // open: clr
  Register register_6 (.D(rom_1_data), .en(decoder_1_out5), .clk(Clock), .Q(Byte5));  // open: clr
  Register register_7 (.D(rom_1_data), .en(decoder_1_out6), .clk(Clock), .Q(Byte6));  // open: clr
  Register register_8 (.D(rom_1_data), .en(decoder_1_out7), .clk(Clock), .Q(Byte7));  // open: clr
  Register register_9 (.D(rom_1_data), .en(decoder_1_out8), .clk(Clock), .Q(Byte8));  // open: clr
  Register register_10 (.D(rom_1_data), .en(decoder_1_out9), .clk(Clock), .Q(Byte9));  // open: clr

  // Notes on the sheet:
  //   contents of rom_1 (hex, n*v repeats v):
  //   30 f4 ff f 6*0 80 14 8*0 30 f7 1 7*0 30 f8 2 7*0 30 f9 3 7*0 30 fa 4 7*0 30 fb 5 7*0 30 fc 6 7*0 30
  //   fd 7 7*0 30 fe 8 7*0 30 f6 1 7*0 20 70 20 b3 20 31 80 65 1 6*0 20 32 20 80 20 d3 20 31 80 65 1 6*0
  //   60 32 30 f1 8*0 40 21 8*0 30 f6 1 7*0 20 70 20 c3 20 31 80 65 1 6*0 20 32 20 80 20 e3 20 31 80 65 1
  //   6*0 60 32 30 f1 8 7*0 40 21 8*0 30 f6 1 7*0 20 90 20 b3 20 31 80 65 1 6*0 20 32 20 a0 20 d3 20 31 80
  //   65 1 6*0 60 32 30 f1 10 7*0 40 21 8*0 30 f6 1 7*0 20 90 20 c3 20 31 80 65 1 6*0 20 32 20 a0 20 e3 20
  //   31 80 65 1 6*0 60 32 30 f1 18 7*0 40 21 8*0 90 61 60 70 70 1 6*0 74 7a 1 6*0 90 60 13 70 65 1
endmodule

module Align (
  input  [7:0] Byte1,
  input  [7:0] Byte2,
  input  [7:0] Byte3,
  input  [7:0] Byte4,
  input  [7:0] Byte5,
  input  [7:0] Byte6,
  input  [7:0] Byte7,
  input  [7:0] Byte8,
  input  [7:0] Byte9,
  input  NeedRegIDs,
  output [3:0] rA,
  output [3:0] rB,
  output [63:0] valC
);

  assign rA = NeedRegIDs ? Byte1[7:4] : 4'bz;  // Controlled_Buffer controlled_buffer_1
  assign rB = NeedRegIDs ? Byte1[3:0] : 4'bz;  // Controlled_Buffer controlled_buffer_2
  Multiplexer #(.width(64)) multiplexer_1 (
    .in0({Byte8, Byte7, Byte6, Byte5, Byte4, Byte3, Byte2, Byte1}),
    .in1({Byte9, Byte8, Byte7, Byte6, Byte5, Byte4, Byte3, Byte2}), .out(valC), .sel(NeedRegIDs));
endmodule

module NeedRegIDs (
  input  [3:0] icode,
  output Need_RegIDs
);

  wire ir_out, mr_out, not_1_out, not_2_out, not_3_out, not_4_out, not_5_out, not_6_out, not_7_out,
       not_8_out, not_9_out, not_10_out, not_11_out, not_12_out, not_13_out, not_14_out, not_15_out,
       not_16_out, not_17_out, not_18_out, not_19_out, not_20_out, not_21_out, not_22_out, not_23_out,
       not_24_out, not_25_out, not_26_out, not_27_out, not_28_out, OPq_out, pop_out, push_out, rm_out, rr_out;

  not not_1 (not_1_out, icode[0]);
  not not_2 (not_2_out, icode[1]);
  not not_3 (not_3_out, icode[2]);
  not not_4 (not_4_out, icode[3]);
  not not_5 (not_5_out, icode[1]);
  not not_6 (not_6_out, icode[2]);
  not not_7 (not_7_out, icode[3]);
  not not_8 (not_8_out, icode[0]);
  not not_9 (not_9_out, icode[2]);
  not not_10 (not_10_out, icode[3]);
  not not_11 (not_11_out, icode[2]);
  not not_12 (not_12_out, icode[3]);
  not not_13 (not_13_out, icode[0]);
  not not_14 (not_14_out, icode[1]);
  not not_15 (not_15_out, icode[3]);
  not not_16 (not_16_out, icode[1]);
  not not_17 (not_17_out, icode[3]);
  not not_18 (not_18_out, icode[0]);
  not not_19 (not_19_out, icode[3]);
  not not_20 (not_20_out, icode[3]);
  not not_21 (not_21_out, icode[0]);
  not not_22 (not_22_out, icode[1]);
  not not_23 (not_23_out, icode[2]);
  not not_24 (not_24_out, icode[1]);
  not not_25 (not_25_out, icode[2]);
  not not_26 (not_26_out, icode[0]);
  not not_27 (not_27_out, icode[2]);
  not not_28 (not_28_out, icode[2]);
  // AND_Gate halt has open pins: in0=not_1_out, in1=not_2_out, in2=not_3_out, in3=not_4_out, out=open
  // AND_Gate nop has open pins: in0=icode[0], in1=not_5_out, in2=not_6_out, in3=not_7_out, out=open
  and rr (rr_out, not_8_out, icode[1], not_9_out, not_10_out);
  and ir (ir_out, icode[0], icode[1], not_11_out, not_12_out);
  and rm (rm_out, not_13_out, not_14_out, icode[2], not_15_out);
  and mr (mr_out, icode[0], not_16_out, icode[2], not_17_out);
  and OPq (OPq_out, not_18_out, icode[1], icode[2], not_19_out);
  // AND_Gate jXX has open pins: in0=icode[0], in1=icode[1], in2=icode[2], in3=not_20_out, out=open
  // AND_Gate call has open pins: in0=not_21_out, in1=not_22_out, in2=not_23_out, in3=icode[3], out=open
  // AND_Gate ret has open pins: in0=icode[0], in1=not_24_out, in2=not_25_out, in3=icode[3], out=open
  and push (push_out, not_26_out, icode[1], not_27_out, icode[3]);
  and pop (pop_out, icode[0], icode[1], not_28_out, icode[3]);
  or or_1 (Need_RegIDs, rr_out, ir_out, rm_out, mr_out, OPq_out, push_out, pop_out);
endmodule

module NeedValC (
  input  [3:0] icode,
  output Need_ValC
);

  wire call_out, ir_out, jXX_out, mr_out, not_1_out, not_2_out, not_3_out, not_4_out, not_5_out, not_6_out,
       not_7_out, not_8_out, not_9_out, not_10_out, not_11_out, not_12_out, not_13_out, not_14_out,
       not_15_out, not_16_out, not_17_out, not_18_out, not_19_out, not_20_out, not_21_out, not_22_out,
       not_23_out, not_24_out, not_25_out, not_26_out, not_27_out, not_28_out, rm_out;

  not not_1 (not_1_out, icode[0]);
  not not_2 (not_2_out, icode[1]);
  not not_3 (not_3_out, icode[2]);
  not not_4 (not_4_out, icode[3]);
  not not_5 (not_5_out, icode[1]);
  not not_6 (not_6_out, icode[2]);
  not not_7 (not_7_out, icode[3]);
  not not_8 (not_8_out, icode[0]);
  not not_9 (not_9_out, icode[2]);
  not not_10 (not_10_out, icode[3]);
  not not_11 (not_11_out, icode[2]);
  not not_12 (not_12_out, icode[3]);
  not not_13 (not_13_out, icode[0]);
  not not_14 (not_14_out, icode[1]);
  not not_15 (not_15_out, icode[3]);
  not not_16 (not_16_out, icode[1]);
  not not_17 (not_17_out, icode[3]);
  not not_18 (not_18_out, icode[0]);
  not not_19 (not_19_out, icode[3]);
  not not_20 (not_20_out, icode[3]);
  not not_21 (not_21_out, icode[0]);
  not not_22 (not_22_out, icode[1]);
  not not_23 (not_23_out, icode[2]);
  not not_24 (not_24_out, icode[1]);
  not not_25 (not_25_out, icode[2]);
  not not_26 (not_26_out, icode[0]);
  not not_27 (not_27_out, icode[2]);
  not not_28 (not_28_out, icode[2]);
  // AND_Gate halt has open pins: in0=not_1_out, in1=not_2_out, in2=not_3_out, in3=not_4_out, out=open
  // AND_Gate nop has open pins: in0=icode[0], in1=not_5_out, in2=not_6_out, in3=not_7_out, out=open
  // AND_Gate rr has open pins: in0=not_8_out, in1=icode[1], in2=not_9_out, in3=not_10_out, out=open
  and ir (ir_out, icode[0], icode[1], not_11_out, not_12_out);
  and rm (rm_out, not_13_out, not_14_out, icode[2], not_15_out);
  and mr (mr_out, icode[0], not_16_out, icode[2], not_17_out);
  // AND_Gate OPq has open pins: in0=not_18_out, in1=icode[1], in2=icode[2], in3=not_19_out, out=open
  and jXX (jXX_out, icode[0], icode[1], icode[2], not_20_out);
  and call (call_out, not_21_out, not_22_out, not_23_out, icode[3]);
  // AND_Gate ret has open pins: in0=icode[0], in1=not_24_out, in2=not_25_out, in3=icode[3], out=open
  // AND_Gate push has open pins: in0=not_26_out, in1=icode[1], in2=not_27_out, in3=icode[3], out=open
  // AND_Gate pop has open pins: in0=icode[0], in1=icode[1], in2=not_28_out, in3=icode[3], out=open
  or or_1 (Need_ValC, ir_out, rm_out, mr_out, jXX_out, call_out);
endmodule

module PCinc (
  input  [63:0] PC,
  input  NeedRegIDS,
  input  NeedValC,
  output [63:0] valP
);

  wire [63:0] adder_1_out, adder_2_out, multiplexer_1_out, multiplexer_2_out;

  Adder #(.width(64)) adder_1 (.a(PC), .b(64'h1), .out(adder_1_out));  // open: cin, cout
  Multiplexer #(.width(64)) multiplexer_1 (.in0({64{1'b0}}), .in1(64'h1), .out(multiplexer_1_out), .sel(NeedRegIDS));
  Adder #(.width(64)) adder_2 (.a(adder_1_out), .b(multiplexer_1_out), .out(adder_2_out));  // open: cin, cout
  Multiplexer #(.width(64)) multiplexer_2 (.in0({64{1'b0}}), .in1(64'h8), .out(multiplexer_2_out), .sel(NeedValC));
  Adder #(.width(64)) adder_3 (.a(adder_2_out), .b(multiplexer_2_out), .out(valP));  // open: cin, cout
endmodule

module Register_File (
  input  [3:0] srcA,
  input  [3:0] srcB,
  input  [63:0] valE,
  input  [63:0] valM,
  input  [3:0] dstE,
  input  [3:0] dstM,
  input  in_7,
  input  in_8,
  input  clk,
  output [63:0] valA,
  output [63:0] valB,
  output [63:0] rax,
  output [63:0] rcx,
  output [63:0] rdx,
  output [63:0] rbx,
  output [63:0] rsp,
  output [63:0] rbp,
  output [63:0] rsi,
  output [63:0] rdi,
  output [63:0] r8,
  output [63:0] r9,
  output [63:0] r10,
  output [63:0] r11,
  output [63:0] r12,
  output [63:0] r13,
  output [63:0] r14
);

  wire decoder_1_out0, decoder_1_out1, decoder_1_out2, decoder_1_out3, decoder_1_out4, decoder_1_out5,
       decoder_1_out6, decoder_1_out7, decoder_1_out8, decoder_1_out9, decoder_1_out10, decoder_1_out11,
       decoder_1_out12, decoder_1_out13, decoder_1_out14, decoder_1_out15, decoder_2_out0, decoder_2_out1,
       decoder_2_out2, decoder_2_out3, decoder_2_out4, decoder_2_out5, decoder_2_out6, decoder_2_out7,
       decoder_2_out8, decoder_2_out9, decoder_2_out10, decoder_2_out11, decoder_2_out12, decoder_2_out13,
       decoder_2_out14, decoder_2_out15, decoder_3_out0, decoder_3_out1, decoder_3_out2, decoder_3_out3,
       decoder_3_out4, decoder_3_out5, decoder_3_out6, decoder_3_out7, decoder_3_out8, decoder_3_out9,
       decoder_3_out10, decoder_3_out11, decoder_3_out12, decoder_3_out13, decoder_3_out14, decoder_4_out0,
       decoder_4_out1, decoder_4_out2, decoder_4_out3, decoder_4_out4, decoder_4_out5, decoder_4_out6,
       decoder_4_out7, decoder_4_out8, decoder_4_out9, decoder_4_out10, decoder_4_out11, decoder_4_out12,
       decoder_4_out13, decoder_4_out14, decoder_4_out15, decoder_5_out0, decoder_5_out1, decoder_5_out2,
       decoder_5_out3, decoder_5_out4, decoder_5_out5, decoder_5_out6, decoder_5_out7, decoder_5_out8,
       decoder_5_out9, decoder_5_out10, decoder_5_out11, decoder_5_out12, decoder_5_out13, decoder_5_out14,
       decoder_5_out15, or_1_out, or_2_out, or_3_out, or_4_out, or_5_out, or_6_out, or_7_out, or_8_out,
       or_9_out, or_10_out, or_11_out, or_12_out, or_13_out, or_14_out, or_15_out, or_16_out, or_17_out;
  wire [3:0] counter_1_q;
  wire [63:0] buffer_1_out, buffer_2_out, buffer_3_out, buffer_4_out, buffer_5_out, buffer_6_out,
       buffer_7_out, buffer_8_out, buffer_9_out, buffer_10_out, buffer_11_out, buffer_12_out, buffer_13_out,
       buffer_14_out, multiplexer_1_out, multiplexer_2_out, multiplexer_3_out, multiplexer_4_out,
       multiplexer_5_out, multiplexer_6_out, multiplexer_7_out, multiplexer_8_out, multiplexer_9_out,
       multiplexer_10_out, multiplexer_11_out, multiplexer_12_out, multiplexer_13_out, multiplexer_14_out,
       multiplexer_15_out, multiplexer_16_out, multiplexer_17_out, register_16_q;

  Decoder #(.enable("false"), .select(4)) decoder_1 (
    .out0(decoder_1_out0), .out1(decoder_1_out1), .out2(decoder_1_out2), .out3(decoder_1_out3),
    .out4(decoder_1_out4), .out5(decoder_1_out5), .out6(decoder_1_out6), .out7(decoder_1_out7),
    .out8(decoder_1_out8), .out9(decoder_1_out9), .out10(decoder_1_out10), .out11(decoder_1_out11),
    .out12(decoder_1_out12), .out13(decoder_1_out13), .out14(decoder_1_out14), .out15(decoder_1_out15),
    .sel(dstE));
  Decoder #(.enable("false"), .select(4)) decoder_2 (
    .out0(decoder_2_out0), .out1(decoder_2_out1), .out2(decoder_2_out2), .out3(decoder_2_out3),
    .out4(decoder_2_out4), .out5(decoder_2_out5), .out6(decoder_2_out6), .out7(decoder_2_out7),
    .out8(decoder_2_out8), .out9(decoder_2_out9), .out10(decoder_2_out10), .out11(decoder_2_out11),
    .out12(decoder_2_out12), .out13(decoder_2_out13), .out14(decoder_2_out14), .out15(decoder_2_out15),
    .sel(dstM));
  assign buffer_1_out = buffer_2_out;  // Buffer buffer_1, 64 bits wide
  assign buffer_2_out = buffer_3_out;  // Buffer buffer_2, 64 bits wide
  assign buffer_3_out = buffer_4_out;  // Buffer buffer_3, 64 bits wide
  assign buffer_4_out = buffer_5_out;  // Buffer buffer_4, 64 bits wide
  assign buffer_5_out = buffer_6_out;  // Buffer buffer_5, 64 bits wide
  assign buffer_6_out = buffer_7_out;  // Buffer buffer_6, 64 bits wide
  assign buffer_7_out = valM;  // Buffer buffer_7, 64 bits wide
  assign buffer_8_out = valE;  // Buffer buffer_8, 64 bits wide
  assign buffer_9_out = buffer_8_out;  // Buffer buffer_9, 64 bits wide
  assign buffer_10_out = buffer_9_out;  // Buffer buffer_10, 64 bits wide
  assign buffer_11_out = buffer_10_out;  // Buffer buffer_11, 64 bits wide
  assign buffer_12_out = buffer_11_out;  // Buffer buffer_12, 64 bits wide
  assign buffer_13_out = buffer_12_out;  // Buffer buffer_13, 64 bits wide
  assign buffer_14_out = buffer_13_out;  // Buffer buffer_14, 64 bits wide
  Multiplexer #(.width(64)) multiplexer_1 (
    .in0(buffer_1_out), .in1(valE), .out(multiplexer_1_out), .sel(decoder_1_out0));
  Multiplexer #(.width(64)) multiplexer_2 (
    .in0(buffer_1_out), .in1(valE), .out(multiplexer_2_out), .sel(decoder_1_out1));
  Multiplexer #(.width(64)) multiplexer_3 (
    .in0(buffer_2_out), .in1(buffer_8_out), .out(multiplexer_3_out), .sel(decoder_1_out2));
  Multiplexer #(.width(64)) multiplexer_4 (
    .in0(buffer_2_out), .in1(buffer_8_out), .out(multiplexer_4_out), .sel(decoder_1_out3));
  Multiplexer #(.width(64)) multiplexer_5 (
    .in0(buffer_3_out), .in1(buffer_9_out), .out(multiplexer_5_out), .sel(decoder_1_out4));
  Multiplexer #(.width(64)) multiplexer_6 (
    .in0(buffer_3_out), .in1(buffer_9_out), .out(multiplexer_6_out), .sel(decoder_1_out5));
  Multiplexer #(.width(64)) multiplexer_7 (
    .in0(buffer_4_out), .in1(buffer_10_out), .out(multiplexer_7_out), .sel(decoder_1_out6));
  Multiplexer #(.width(64)) multiplexer_8 (
    .in0(buffer_4_out), .in1(buffer_10_out), .out(multiplexer_8_out), .sel(decoder_1_out7));
  Multiplexer #(.width(64)) multiplexer_9 (
    .in0(buffer_5_out), .in1(buffer_11_out), .out(multiplexer_9_out), .sel(decoder_1_out8));
  Multiplexer #(.width(64)) multiplexer_10 (
    .in0(buffer_5_out), .in1(buffer_11_out), .out(multiplexer_10_out), .sel(decoder_1_out9));
  Multiplexer #(.width(64)) multiplexer_11 (
    .in0(buffer_6_out), .in1(buffer_12_out), .out(multiplexer_11_out), .sel(decoder_1_out10));
  Multiplexer #(.width(64)) multiplexer_12 (
    .in0(buffer_6_out), .in1(buffer_12_out), .out(multiplexer_12_out), .sel(decoder_1_out11));
  Multiplexer #(.width(64)) multiplexer_13 (
    .in0(buffer_7_out), .in1(buffer_13_out), .out(multiplexer_13_out), .sel(decoder_1_out12));
  Multiplexer #(.width(64)) multiplexer_14 (
    .in0(buffer_7_out), .in1(buffer_13_out), .out(multiplexer_14_out), .sel(decoder_1_out13));
  Multiplexer #(.width(64)) multiplexer_15 (
    .in0(valM), .in1(buffer_14_out), .out(multiplexer_15_out), .sel(decoder_1_out14));
  Multiplexer #(.width(64)) multiplexer_16 (
    .in0(valM), .in1(buffer_14_out), .out(multiplexer_16_out), .sel(decoder_1_out15));
  Multiplexer #(.width(64)) multiplexer_17 (
    .in0(multiplexer_5_out), .in1(64'hfff), .out(multiplexer_17_out), .sel(in_7));
  Counter #(.max('hd), .width(4)) counter_1 (.Q(counter_1_q), .clk(clk));  // open: load, D, count, carry, up, clr
  Decoder #(.enable("false"), .select(4)) decoder_3 (
    .out0(decoder_3_out0), .out1(decoder_3_out1), .out2(decoder_3_out2), .out3(decoder_3_out3),
    .out4(decoder_3_out4), .out5(decoder_3_out5), .out6(decoder_3_out6), .out7(decoder_3_out7),
    .out8(decoder_3_out8), .out9(decoder_3_out9), .out10(decoder_3_out10), .out11(decoder_3_out11),
    .out12(decoder_3_out12), .out13(decoder_3_out13), .out14(decoder_3_out14), .sel(counter_1_q));  // open: out15
  or or_1 (or_1_out, decoder_1_out0, decoder_2_out0);
  or or_2 (or_2_out, decoder_1_out1, decoder_2_out1);
  or or_3 (or_3_out, decoder_1_out2, decoder_2_out2);
  or or_4 (or_4_out, decoder_1_out3, decoder_2_out3);
  or or_5 (or_5_out, decoder_1_out4, in_7, decoder_2_out4);
  or or_6 (or_6_out, decoder_1_out5, decoder_2_out5);
  or or_7 (or_7_out, decoder_1_out6, decoder_2_out6);
  or or_8 (or_8_out, decoder_1_out7, decoder_2_out7);
  or or_9 (or_9_out, decoder_1_out8, decoder_2_out8);
  or or_10 (or_10_out, decoder_1_out9, decoder_2_out9);
  or or_11 (or_11_out, decoder_1_out10, decoder_2_out10);
  or or_12 (or_12_out, decoder_1_out11, decoder_2_out11);
  or or_13 (or_13_out, decoder_1_out12, decoder_2_out12);
  or or_14 (or_14_out, decoder_1_out13, decoder_2_out13);
  or or_15 (or_15_out, decoder_1_out14, decoder_2_out14);
  or or_16 (or_16_out, decoder_1_out15, decoder_2_out15);
  or or_17 (or_17_out, decoder_3_out13, in_8);
  Register #(.width(64)) register_1 (.D(multiplexer_1_out), .en(or_1_out), .clk(or_17_out), .Q(rax));  // open: clr
  Register #(.width(64)) register_2 (.D(multiplexer_2_out), .en(or_2_out), .clk(or_17_out), .Q(rcx));  // open: clr
  Register #(.width(64)) register_3 (.D(multiplexer_3_out), .en(or_3_out), .clk(or_17_out), .Q(rdx));  // open: clr
  Register #(.width(64)) register_4 (.D(multiplexer_4_out), .en(or_4_out), .clk(or_17_out), .Q(rbx));  // open: clr
  Register #(.width(64)) register_5 (.D(multiplexer_17_out), .en(or_5_out), .clk(or_17_out), .Q(rsp));  // open: clr
  Register #(.width(64)) register_6 (.D(multiplexer_6_out), .en(or_6_out), .clk(or_17_out), .Q(rbp));  // open: clr
  Register #(.width(64)) register_7 (.D(multiplexer_7_out), .en(or_7_out), .clk(or_17_out), .Q(rsi));  // open: clr
  Register #(.width(64)) register_8 (.D(multiplexer_8_out), .en(or_8_out), .clk(or_17_out), .Q(rdi));  // open: clr
  Register #(.width(64)) register_9 (.D(multiplexer_9_out), .en(or_9_out), .clk(or_17_out), .Q(r8));  // open: clr
  Register #(.width(64)) register_10 (.D(multiplexer_10_out), .en(or_10_out), .clk(or_17_out), .Q(r9));  // open: clr
  Register #(.width(64)) register_11 (.D(multiplexer_11_out), .en(or_11_out), .clk(or_17_out), .Q(r10));  // open: clr
  Register #(.width(64)) register_12 (.D(multiplexer_12_out), .en(or_12_out), .clk(or_17_out), .Q(r11));  // open: clr
  Register #(.width(64)) register_13 (.D(multiplexer_13_out), .en(or_13_out), .clk(or_17_out), .Q(r12));  // open: clr
  Register #(.width(64)) register_14 (.D(multiplexer_14_out), .en(or_14_out), .clk(or_17_out), .Q(r13));  // open: clr
  Register #(.width(64)) register_15 (.D(multiplexer_15_out), .en(or_15_out), .clk(or_17_out), .Q(r14));  // open: clr
  Register #(.width(64)) register_16 (
    .D(multiplexer_16_out), .en(or_16_out), .clk(or_17_out), .Q(register_16_q));  // open: clr
  assign valA = decoder_4_out0 ? rax : 64'bz;  // Controlled_Buffer controlled_buffer_1
  assign valA = decoder_4_out1 ? rcx : 64'bz;  // Controlled_Buffer controlled_buffer_2
  assign valA = decoder_4_out2 ? rdx : 64'bz;  // Controlled_Buffer controlled_buffer_3
  assign valA = decoder_4_out3 ? rbx : 64'bz;  // Controlled_Buffer controlled_buffer_4
  assign valA = decoder_4_out4 ? rsp : 64'bz;  // Controlled_Buffer controlled_buffer_5
  assign valA = decoder_4_out5 ? rbp : 64'bz;  // Controlled_Buffer controlled_buffer_6
  assign valA = decoder_4_out6 ? rsi : 64'bz;  // Controlled_Buffer controlled_buffer_7
  assign valA = decoder_4_out7 ? rdi : 64'bz;  // Controlled_Buffer controlled_buffer_8
  assign valA = decoder_4_out8 ? r8 : 64'bz;  // Controlled_Buffer controlled_buffer_9
  assign valA = decoder_4_out9 ? r9 : 64'bz;  // Controlled_Buffer controlled_buffer_10
  assign valA = decoder_4_out10 ? r10 : 64'bz;  // Controlled_Buffer controlled_buffer_11
  assign valA = decoder_4_out11 ? r11 : 64'bz;  // Controlled_Buffer controlled_buffer_12
  assign valA = decoder_4_out12 ? r12 : 64'bz;  // Controlled_Buffer controlled_buffer_13
  assign valA = decoder_4_out13 ? r13 : 64'bz;  // Controlled_Buffer controlled_buffer_14
  assign valA = decoder_4_out14 ? r14 : 64'bz;  // Controlled_Buffer controlled_buffer_15
  assign valA = decoder_4_out15 ? register_16_q : 64'bz;  // Controlled_Buffer controlled_buffer_16
  Decoder #(.enable("false"), .select(4)) decoder_4 (
    .out0(decoder_4_out0), .out1(decoder_4_out1), .out2(decoder_4_out2), .out3(decoder_4_out3),
    .out4(decoder_4_out4), .out5(decoder_4_out5), .out6(decoder_4_out6), .out7(decoder_4_out7),
    .out8(decoder_4_out8), .out9(decoder_4_out9), .out10(decoder_4_out10), .out11(decoder_4_out11),
    .out12(decoder_4_out12), .out13(decoder_4_out13), .out14(decoder_4_out14), .out15(decoder_4_out15),
    .sel(srcA));
  assign valB = decoder_5_out0 ? rax : 64'bz;  // Controlled_Buffer controlled_buffer_17
  assign valB = decoder_5_out1 ? rcx : 64'bz;  // Controlled_Buffer controlled_buffer_18
  assign valB = decoder_5_out2 ? rdx : 64'bz;  // Controlled_Buffer controlled_buffer_19
  assign valB = decoder_5_out3 ? rbx : 64'bz;  // Controlled_Buffer controlled_buffer_20
  assign valB = decoder_5_out4 ? rsp : 64'bz;  // Controlled_Buffer controlled_buffer_21
  assign valB = decoder_5_out5 ? rbp : 64'bz;  // Controlled_Buffer controlled_buffer_22
  assign valB = decoder_5_out6 ? rsi : 64'bz;  // Controlled_Buffer controlled_buffer_23
  assign valB = decoder_5_out7 ? rdi : 64'bz;  // Controlled_Buffer controlled_buffer_24
  assign valB = decoder_5_out8 ? r8 : 64'bz;  // Controlled_Buffer controlled_buffer_25
  assign valB = decoder_5_out9 ? r9 : 64'bz;  // Controlled_Buffer controlled_buffer_26
  assign valB = decoder_5_out10 ? r10 : 64'bz;  // Controlled_Buffer controlled_buffer_27
  assign valB = decoder_5_out11 ? r11 : 64'bz;  // Controlled_Buffer controlled_buffer_28
  assign valB = decoder_5_out12 ? r12 : 64'bz;  // Controlled_Buffer controlled_buffer_29
  assign valB = decoder_5_out13 ? r13 : 64'bz;  // Controlled_Buffer controlled_buffer_30
  assign valB = decoder_5_out14 ? r14 : 64'bz;  // Controlled_Buffer controlled_buffer_31
  assign valB = decoder_5_out15 ? register_16_q : 64'bz;  // Controlled_Buffer controlled_buffer_32
  Decoder #(.enable("false"), .select(4)) decoder_5 (
    .out0(decoder_5_out0), .out1(decoder_5_out1), .out2(decoder_5_out2), .out3(decoder_5_out3),
    .out4(decoder_5_out4), .out5(decoder_5_out5), .out6(decoder_5_out6), .out7(decoder_5_out7),
    .out8(decoder_5_out8), .out9(decoder_5_out9), .out10(decoder_5_out10), .out11(decoder_5_out11),
    .out12(decoder_5_out12), .out13(decoder_5_out13), .out14(decoder_5_out14), .out15(decoder_5_out15),
    .sel(srcB));

  // Notes on the sheet:
  //   Write Port 1
  //   Write Port 2
  //   Read Port 1
  //   Read Port 2
endmodule

module srcA (
  input  [3:0] icode,
  input  [3:0] rA,
  output [3:0] sA
);

  wire not_1_out, not_2_out, not_3_out, not_4_out, not_5_out, not_6_out, not_7_out, not_8_out, not_9_out,
       not_10_out, not_11_out, not_12_out, not_13_out, not_14_out, not_15_out, not_16_out, not_17_out,
       not_18_out, not_19_out, not_20_out, not_21_out, not_22_out, not_23_out, not_24_out, not_25_out,
       not_26_out, not_27_out, not_28_out, OPq_out, pop_out, push_out, ret_out, rm_out, rr_out;
  wire [1:0] or_1_out;

  not not_1 (not_1_out, icode[0]);
  not not_2 (not_2_out, icode[1]);
  not not_3 (not_3_out, icode[2]);
  not not_4 (not_4_out, icode[3]);
  not not_5 (not_5_out, icode[1]);
  not not_6 (not_6_out, icode[2]);
  not not_7 (not_7_out, icode[3]);
  not not_8 (not_8_out, icode[0]);
  not not_9 (not_9_out, icode[2]);
  not not_10 (not_10_out, icode[3]);
  not not_11 (not_11_out, icode[2]);
  not not_12 (not_12_out, icode[3]);
  not not_13 (not_13_out, icode[0]);
  not not_14 (not_14_out, icode[1]);
  not not_15 (not_15_out, icode[3]);
  not not_16 (not_16_out, icode[1]);
  not not_17 (not_17_out, icode[3]);
  not not_18 (not_18_out, icode[0]);
  not not_19 (not_19_out, icode[3]);
  not not_20 (not_20_out, icode[3]);
  not not_21 (not_21_out, icode[0]);
  not not_22 (not_22_out, icode[1]);
  not not_23 (not_23_out, icode[2]);
  not not_24 (not_24_out, icode[1]);
  not not_25 (not_25_out, icode[2]);
  not not_26 (not_26_out, icode[0]);
  not not_27 (not_27_out, icode[2]);
  not not_28 (not_28_out, icode[2]);
  // AND_Gate halt has open pins: in0=not_1_out, in1=not_2_out, in2=not_3_out, in3=not_4_out, out=open
  // AND_Gate nop has open pins: in0=icode[0], in1=not_5_out, in2=not_6_out, in3=not_7_out, out=open
  and rr (rr_out, not_8_out, icode[1], not_9_out, not_10_out);
  // AND_Gate ir has open pins: in0=icode[0], in1=icode[1], in2=not_11_out, in3=not_12_out, out=open
  and rm (rm_out, not_13_out, not_14_out, icode[2], not_15_out);
  // AND_Gate mr has open pins: in0=icode[0], in1=not_16_out, in2=icode[2], in3=not_17_out, out=open
  and OPq (OPq_out, not_18_out, icode[1], icode[2], not_19_out);
  // AND_Gate jXX has open pins: in0=icode[0], in1=icode[1], in2=icode[2], in3=not_20_out, out=open
  // AND_Gate call has open pins: in0=not_21_out, in1=not_22_out, in2=not_23_out, in3=icode[3], out=open
  and ret (ret_out, icode[0], not_24_out, not_25_out, icode[3]);
  and push (push_out, not_26_out, icode[1], not_27_out, icode[3]);
  and pop (pop_out, icode[0], icode[1], not_28_out, icode[3]);
  or or_1 (or_1_out[0], rr_out, rm_out, OPq_out, push_out);
  or or_2 (or_1_out[1], ret_out, pop_out);
  Multiplexer #(.select(2), .width(4)) multiplexer_1 (
    .in0(4'b1111), .in1(rA), .in2(4'b0100), .out(sA), .sel(or_1_out));  // open: in3
endmodule

module srcB (
  input  [3:0] icode,
  input  [3:0] rB,
  output [3:0] sB
);

  wire call_out, mr_out, not_1_out, not_2_out, not_3_out, not_4_out, not_5_out, not_6_out, not_7_out,
       not_8_out, not_9_out, not_10_out, not_11_out, not_12_out, not_13_out, not_14_out, not_15_out,
       not_16_out, not_17_out, not_18_out, not_19_out, not_20_out, not_21_out, not_22_out, not_23_out,
       not_24_out, not_25_out, not_26_out, not_27_out, not_28_out, OPq_out, pop_out, push_out, ret_out,
       rm_out, rr_out;
  wire [1:0] or_1_out;

  not not_1 (not_1_out, icode[0]);
  not not_2 (not_2_out, icode[1]);
  not not_3 (not_3_out, icode[2]);
  not not_4 (not_4_out, icode[3]);
  not not_5 (not_5_out, icode[1]);
  not not_6 (not_6_out, icode[2]);
  not not_7 (not_7_out, icode[3]);
  not not_8 (not_8_out, icode[0]);
  not not_9 (not_9_out, icode[2]);
  not not_10 (not_10_out, icode[3]);
  not not_11 (not_11_out, icode[2]);
  not not_12 (not_12_out, icode[3]);
  not not_13 (not_13_out, icode[0]);
  not not_14 (not_14_out, icode[1]);
  not not_15 (not_15_out, icode[3]);
  not not_16 (not_16_out, icode[1]);
  not not_17 (not_17_out, icode[3]);
  not not_18 (not_18_out, icode[0]);
  not not_19 (not_19_out, icode[3]);
  not not_20 (not_20_out, icode[3]);
  not not_21 (not_21_out, icode[0]);
  not not_22 (not_22_out, icode[1]);
  not not_23 (not_23_out, icode[2]);
  not not_24 (not_24_out, icode[1]);
  not not_25 (not_25_out, icode[2]);
  not not_26 (not_26_out, icode[0]);
  not not_27 (not_27_out, icode[2]);
  not not_28 (not_28_out, icode[2]);
  // AND_Gate halt has open pins: in0=not_1_out, in1=not_2_out, in2=not_3_out, in3=not_4_out, out=open
  // AND_Gate nop has open pins: in0=icode[0], in1=not_5_out, in2=not_6_out, in3=not_7_out, out=open
  and rr (rr_out, not_8_out, icode[1], not_9_out, not_10_out);
  // AND_Gate ir has open pins: in0=icode[0], in1=icode[1], in2=not_11_out, in3=not_12_out, out=open
  and rm (rm_out, not_13_out, not_14_out, icode[2], not_15_out);
  and mr (mr_out, icode[0], not_16_out, icode[2], not_17_out);
  and OPq (OPq_out, not_18_out, icode[1], icode[2], not_19_out);
  // AND_Gate jXX has open pins: in0=icode[0], in1=icode[1], in2=icode[2], in3=not_20_out, out=open
  and call (call_out, not_21_out, not_22_out, not_23_out, icode[3]);
  and ret (ret_out, icode[0], not_24_out, not_25_out, icode[3]);
  and push (push_out, not_26_out, icode[1], not_27_out, icode[3]);
  and pop (pop_out, icode[0], icode[1], not_28_out, icode[3]);
  or or_1 (or_1_out[0], rr_out, rm_out, mr_out, OPq_out);
  or or_2 (or_1_out[1], call_out, ret_out, push_out, pop_out);
  Multiplexer #(.select(2), .width(4)) multiplexer_1 (
    .in0(4'b1111), .in1(rB), .in2(4'b0100), .out(sB), .sel(or_1_out));  // open: in3
endmodule

module dstE (
  input  [3:0] icode,
  input  [3:0] rB,
  output [3:0] dE
);

  wire call_out, ir_out, not_1_out, not_2_out, not_3_out, not_4_out, not_5_out, not_6_out, not_7_out,
       not_8_out, not_9_out, not_10_out, not_11_out, not_12_out, not_13_out, not_14_out, not_15_out,
       not_16_out, not_17_out, not_18_out, not_19_out, not_20_out, not_21_out, not_22_out, not_23_out,
       not_24_out, not_25_out, not_26_out, not_27_out, not_28_out, OPq_out, pop_out, push_out, ret_out,
       rr_out;
  wire [1:0] or_1_out;

  not not_1 (not_1_out, icode[0]);
  not not_2 (not_2_out, icode[1]);
  not not_3 (not_3_out, icode[2]);
  not not_4 (not_4_out, icode[3]);
  not not_5 (not_5_out, icode[1]);
  not not_6 (not_6_out, icode[2]);
  not not_7 (not_7_out, icode[3]);
  not not_8 (not_8_out, icode[0]);
  not not_9 (not_9_out, icode[2]);
  not not_10 (not_10_out, icode[3]);
  not not_11 (not_11_out, icode[2]);
  not not_12 (not_12_out, icode[3]);
  not not_13 (not_13_out, icode[0]);
  not not_14 (not_14_out, icode[1]);
  not not_15 (not_15_out, icode[3]);
  not not_16 (not_16_out, icode[1]);
  not not_17 (not_17_out, icode[3]);
  not not_18 (not_18_out, icode[0]);
  not not_19 (not_19_out, icode[3]);
  not not_20 (not_20_out, icode[3]);
  not not_21 (not_21_out, icode[0]);
  not not_22 (not_22_out, icode[1]);
  not not_23 (not_23_out, icode[2]);
  not not_24 (not_24_out, icode[1]);
  not not_25 (not_25_out, icode[2]);
  not not_26 (not_26_out, icode[0]);
  not not_27 (not_27_out, icode[2]);
  not not_28 (not_28_out, icode[2]);
  // AND_Gate halt has open pins: in0=not_1_out, in1=not_2_out, in2=not_3_out, in3=not_4_out, out=open
  // AND_Gate nop has open pins: in0=icode[0], in1=not_5_out, in2=not_6_out, in3=not_7_out, out=open
  and rr (rr_out, not_8_out, icode[1], not_9_out, not_10_out);
  and ir (ir_out, icode[0], icode[1], not_11_out, not_12_out);
  // AND_Gate rm has open pins: in0=not_13_out, in1=not_14_out, in2=icode[2], in3=not_15_out, out=open
  // AND_Gate mr has open pins: in0=icode[0], in1=not_16_out, in2=icode[2], in3=not_17_out, out=open
  and OPq (OPq_out, not_18_out, icode[1], icode[2], not_19_out);
  // AND_Gate jXX has open pins: in0=icode[0], in1=icode[1], in2=icode[2], in3=not_20_out, out=open
  and call (call_out, not_21_out, not_22_out, not_23_out, icode[3]);
  and ret (ret_out, icode[0], not_24_out, not_25_out, icode[3]);
  and push (push_out, not_26_out, icode[1], not_27_out, icode[3]);
  and pop (pop_out, icode[0], icode[1], not_28_out, icode[3]);
  or or_1 (or_1_out[0], rr_out, ir_out, OPq_out);
  or or_2 (or_1_out[1], call_out, ret_out, push_out, pop_out);
  Multiplexer #(.select(2), .width(4)) multiplexer_1 (
    .in0(4'b1111), .in1(rB), .in2(4'b0100), .out(dE), .sel(or_1_out));  // open: in3
endmodule

module dstM (
  input  [3:0] icode,
  input  [3:0] rA,
  output [3:0] dM
);

  wire mr_out, not_1_out, not_2_out, not_3_out, not_4_out, not_5_out, not_6_out, not_7_out, not_8_out,
       not_9_out, not_10_out, not_11_out, not_12_out, not_13_out, not_14_out, not_15_out, not_16_out,
       not_17_out, not_18_out, not_19_out, not_20_out, not_21_out, not_22_out, not_23_out, not_24_out,
       not_25_out, not_26_out, not_27_out, not_28_out, pop_out;
  wire [0:0] or_1_out;

  not not_1 (not_1_out, icode[0]);
  not not_2 (not_2_out, icode[1]);
  not not_3 (not_3_out, icode[2]);
  not not_4 (not_4_out, icode[3]);
  not not_5 (not_5_out, icode[1]);
  not not_6 (not_6_out, icode[2]);
  not not_7 (not_7_out, icode[3]);
  not not_8 (not_8_out, icode[0]);
  not not_9 (not_9_out, icode[2]);
  not not_10 (not_10_out, icode[3]);
  not not_11 (not_11_out, icode[2]);
  not not_12 (not_12_out, icode[3]);
  not not_13 (not_13_out, icode[0]);
  not not_14 (not_14_out, icode[1]);
  not not_15 (not_15_out, icode[3]);
  not not_16 (not_16_out, icode[1]);
  not not_17 (not_17_out, icode[3]);
  not not_18 (not_18_out, icode[0]);
  not not_19 (not_19_out, icode[3]);
  not not_20 (not_20_out, icode[3]);
  not not_21 (not_21_out, icode[0]);
  not not_22 (not_22_out, icode[1]);
  not not_23 (not_23_out, icode[2]);
  not not_24 (not_24_out, icode[1]);
  not not_25 (not_25_out, icode[2]);
  not not_26 (not_26_out, icode[0]);
  not not_27 (not_27_out, icode[2]);
  not not_28 (not_28_out, icode[2]);
  // AND_Gate halt has open pins: in0=not_1_out, in1=not_2_out, in2=not_3_out, in3=not_4_out, out=open
  // AND_Gate nop has open pins: in0=icode[0], in1=not_5_out, in2=not_6_out, in3=not_7_out, out=open
  // AND_Gate rr has open pins: in0=not_8_out, in1=icode[1], in2=not_9_out, in3=not_10_out, out=open
  // AND_Gate ir has open pins: in0=icode[0], in1=icode[1], in2=not_11_out, in3=not_12_out, out=open
  // AND_Gate rm has open pins: in0=not_13_out, in1=not_14_out, in2=icode[2], in3=not_15_out, out=open
  and mr (mr_out, icode[0], not_16_out, icode[2], not_17_out);
  // AND_Gate OPq has open pins: in0=not_18_out, in1=icode[1], in2=icode[2], in3=not_19_out, out=open
  // AND_Gate jXX has open pins: in0=icode[0], in1=icode[1], in2=icode[2], in3=not_20_out, out=open
  // AND_Gate call has open pins: in0=not_21_out, in1=not_22_out, in2=not_23_out, in3=icode[3], out=open
  // AND_Gate ret has open pins: in0=icode[0], in1=not_24_out, in2=not_25_out, in3=icode[3], out=open
  // AND_Gate push has open pins: in0=not_26_out, in1=icode[1], in2=not_27_out, in3=icode[3], out=open
  and pop (pop_out, icode[0], icode[1], not_28_out, icode[3]);
  or or_1 (or_1_out[0], mr_out, pop_out);
  Multiplexer #(.select(2), .width(4)) multiplexer_1 (
    .in0(4'b1111), .in1(rA), .in2(4'b0100), .out(dM), .sel({1'b0, or_1_out[0]}));  // open: in3
endmodule

module ALU (
  input  [1:0] ALUfunc,
  input  [63:0] AluA,
  input  [63:0] AluB,
  input  Clk,
  output [63:0] valE,
  output [2:0] ZSO
);

  wire and_2_out, and_3_out, and_4_out, comparator_1_gt, comparator_1_lt, comparator_2_gt, comparator_2_lt,
       comparator_3_gt, comparator_3_lt, decoder_1_out0, decoder_1_out1, decoder_1_out2, decoder_1_out3,
       decoder_1_out4, decoder_1_out5, decoder_1_out6, decoder_1_out7, decoder_1_out8, decoder_1_out9,
       decoder_1_out10, decoder_1_out11, decoder_1_out12, decoder_1_out13, decoder_1_out14, decoder_1_out15,
       not_1_out, subtractor_1_bout;
  wire [2:0] or_2_out;
  wire [3:0] counter_1_q;
  wire [63:0] adder_1_out, and_1_out, multiplexer_1_out, subtractor_1_out, xor_1_out;

  Comparator #(.width(64)) comparator_1 (
    .a(AluB), .b({64{1'b0}}), .gt(comparator_1_gt), .lt(comparator_1_lt));  // open: eq
  Comparator #(.width(64)) comparator_2 (
    .a(AluA), .b({64{1'b0}}), .gt(comparator_2_gt), .lt(comparator_2_lt));  // open: eq
  Adder #(.width(64)) adder_1 (.a(AluA), .b(AluB), .out(adder_1_out));  // open: cin, cout
  Subtractor #(.width(64)) subtractor_1 (
    .a(AluB), .b(AluA), .out(subtractor_1_out), .bout(subtractor_1_bout));  // open: bin
  assign and_1_out = AluB & AluA;  // AND_Gate and_1, 64 bits wide
  assign xor_1_out = AluB ^ AluA;  // XOR_Gate xor_1, 64 bits wide
  not not_1 (not_1_out, ALUfunc[1]);
  and and_2 (and_2_out, ALUfunc[0], not_1_out, subtractor_1_bout);
  Multiplexer #(.select(2), .width(64)) multiplexer_1 (
    .in0(adder_1_out), .in1(subtractor_1_out), .in2(and_1_out), .in3(xor_1_out), .out(multiplexer_1_out),
    .sel(ALUfunc));
  Comparator #(.width(64)) comparator_3 (
    .a(multiplexer_1_out), .b({64{1'b0}}), .gt(comparator_3_gt), .eq(or_2_out[2]), .lt(comparator_3_lt));
  and and_3 (and_3_out, comparator_1_gt, comparator_3_lt, comparator_2_gt);
  and and_4 (and_4_out, comparator_1_lt, comparator_2_lt, comparator_3_gt);
  or or_1 (or_2_out[1], and_2_out, comparator_3_lt);
  or or_2 (or_2_out[0], and_4_out, and_3_out);
  Decoder #(.enable("false"), .select(4)) decoder_1 (
    .out0(decoder_1_out0), .out1(decoder_1_out1), .out2(decoder_1_out2), .out3(decoder_1_out3),
    .out4(decoder_1_out4), .out5(decoder_1_out5), .out6(decoder_1_out6), .out7(decoder_1_out7),
    .out8(decoder_1_out8), .out9(decoder_1_out9), .out10(decoder_1_out10), .out11(decoder_1_out11),
    .out12(decoder_1_out12), .out13(decoder_1_out13), .out14(decoder_1_out14), .out15(decoder_1_out15),
    .sel(counter_1_q));
  Counter #(.max('hd), .width(4)) counter_1 (.Q(counter_1_q), .clk(Clk));  // open: load, D, count, carry, up, clr
  Register #(.width(64)) register_1 (.D(multiplexer_1_out), .en(decoder_1_out10), .clk(Clk), .Q(valE));  // open: clr
  Register #(.width(3)) register_2 (.D(or_2_out), .en(decoder_1_out10), .clk(Clk), .Q(ZSO));  // open: clr

  // Notes on the sheet:
  //   0-add        1-subtract         2-and         3-xor
endmodule

module ALUA (
  input  [63:0] valA,
  input  [63:0] valC,
  input  [3:0] icode,
  output [63:0] out_4
);

  wire call_out, ir_out, mr_out, not_1_out, not_2_out, not_3_out, not_4_out, not_5_out, not_6_out, not_7_out,
       not_8_out, not_9_out, not_10_out, not_11_out, not_12_out, not_13_out, not_14_out, not_15_out,
       not_16_out, not_17_out, not_18_out, not_19_out, not_20_out, opq_out, or_1_out, or_2_out, or_3_out,
       pop_out, push_out, ret_out, rm_out, rr_out;
  wire [1:0] or_4_out;

  not not_1 (not_1_out, icode[0]);
  not not_2 (not_2_out, icode[2]);
  not not_3 (not_3_out, icode[3]);
  not not_4 (not_4_out, icode[0]);
  not not_5 (not_5_out, icode[3]);
  not not_6 (not_6_out, icode[2]);
  not not_7 (not_7_out, icode[3]);
  not not_8 (not_8_out, icode[0]);
  not not_9 (not_9_out, icode[1]);
  not not_10 (not_10_out, icode[3]);
  not not_11 (not_11_out, icode[1]);
  not not_12 (not_12_out, icode[3]);
  not not_13 (not_13_out, icode[0]);
  not not_14 (not_14_out, icode[1]);
  not not_15 (not_15_out, icode[2]);
  not not_16 (not_16_out, icode[1]);
  not not_17 (not_17_out, icode[2]);
  not not_18 (not_18_out, icode[0]);
  not not_19 (not_19_out, icode[2]);
  not not_20 (not_20_out, icode[2]);
  and rr (rr_out, not_1_out, icode[1], not_2_out, not_3_out);
  and opq (opq_out, not_4_out, icode[1], icode[2], not_5_out);
  and ir (ir_out, icode[0], icode[1], not_6_out, not_7_out);
  and rm (rm_out, not_8_out, not_9_out, icode[2], not_10_out);
  and mr (mr_out, icode[0], not_11_out, icode[2], not_12_out);
  and call (call_out, not_13_out, not_14_out, not_15_out, icode[3]);
  and ret (ret_out, icode[0], not_16_out, not_17_out, icode[3]);
  and push (push_out, not_18_out, icode[1], not_19_out, icode[3]);
  and pop (pop_out, icode[0], icode[1], not_20_out, icode[3]);
  or or_1 (or_1_out, rr_out, opq_out);
  or or_2 (or_2_out, ir_out, rm_out, mr_out);
  or or_3 (or_3_out, call_out, ret_out, push_out, pop_out);
  or or_4 (or_4_out[0], or_1_out, or_3_out);
  or or_5 (or_4_out[1], or_2_out, or_3_out);
  Multiplexer #(.select(2), .width(64)) multiplexer_1 (
    .in1(valA), .in2(valC), .in3(64'h8), .out(out_4), .sel(or_4_out));  // open: in0
endmodule

module ALUB (
  input  [63:0] valB,
  input  [3:0] icode,
  output [63:0] out_3
);

  wire call_out, ir_out, mr_out, not_1_out, not_2_out, not_3_out, not_4_out, not_5_out, not_6_out, not_7_out,
       not_8_out, not_9_out, not_10_out, not_11_out, not_12_out, not_13_out, not_14_out, not_15_out,
       not_16_out, not_17_out, not_18_out, not_19_out, not_20_out, opq_out, pop_out, push_out, ret_out,
       rm_out, rr_out;
  wire [1:0] or_1_out;

  not not_1 (not_1_out, icode[0]);
  not not_2 (not_2_out, icode[2]);
  not not_3 (not_3_out, icode[3]);
  not not_4 (not_4_out, icode[2]);
  not not_5 (not_5_out, icode[3]);
  not not_6 (not_6_out, icode[0]);
  not not_7 (not_7_out, icode[3]);
  not not_8 (not_8_out, icode[0]);
  not not_9 (not_9_out, icode[1]);
  not not_10 (not_10_out, icode[3]);
  not not_11 (not_11_out, icode[1]);
  not not_12 (not_12_out, icode[3]);
  not not_13 (not_13_out, icode[0]);
  not not_14 (not_14_out, icode[1]);
  not not_15 (not_15_out, icode[2]);
  not not_16 (not_16_out, icode[1]);
  not not_17 (not_17_out, icode[2]);
  not not_18 (not_18_out, icode[0]);
  not not_19 (not_19_out, icode[2]);
  not not_20 (not_20_out, icode[2]);
  and rr (rr_out, not_1_out, icode[1], not_2_out, not_3_out);
  and ir (ir_out, icode[0], icode[1], not_4_out, not_5_out);
  and opq (opq_out, not_6_out, icode[1], icode[2], not_7_out);
  and rm (rm_out, not_8_out, not_9_out, icode[2], not_10_out);
  and mr (mr_out, icode[0], not_11_out, icode[2], not_12_out);
  and call (call_out, not_13_out, not_14_out, not_15_out, icode[3]);
  and ret (ret_out, icode[0], not_16_out, not_17_out, icode[3]);
  and push (push_out, not_18_out, icode[1], not_19_out, icode[3]);
  and pop (pop_out, icode[0], icode[1], not_20_out, icode[3]);
  or or_1 (or_1_out[0], rr_out, ir_out);
  or or_2 (or_1_out[1], opq_out, rm_out, mr_out, call_out, ret_out, push_out, pop_out);
  Multiplexer #(.select(2), .width(64)) multiplexer_1 (
    .in1({64{1'b0}}), .in2(valB), .out(out_3), .sel(or_1_out));  // open: in0, in3
endmodule

module ALUfunc (
  input  [3:0] icode,
  input  [3:0] ifun,
  output [1:0] alufun
);

  wire and_1_out, and_2_out, and_3_out, call_out, not_1_out, not_2_out, not_3_out, not_4_out, not_5_out,
       not_6_out, not_7_out, not_8_out, not_9_out, not_10_out, not_11_out, not_12_out, not_13_out,
       not_14_out, not_15_out, not_16_out, not_17_out, not_18_out, not_19_out, not_20_out, not_21_out,
       not_22_out, not_23_out, not_24_out, not_25_out, not_26_out, not_27_out, not_28_out, OPq_out, push_out;

  not not_1 (not_1_out, icode[0]);
  not not_2 (not_2_out, icode[1]);
  not not_3 (not_3_out, icode[2]);
  not not_4 (not_4_out, icode[3]);
  not not_5 (not_5_out, icode[1]);
  not not_6 (not_6_out, icode[2]);
  not not_7 (not_7_out, icode[3]);
  not not_8 (not_8_out, icode[0]);
  not not_9 (not_9_out, icode[2]);
  not not_10 (not_10_out, icode[3]);
  not not_11 (not_11_out, icode[2]);
  not not_12 (not_12_out, icode[3]);
  not not_13 (not_13_out, icode[0]);
  not not_14 (not_14_out, icode[1]);
  not not_15 (not_15_out, icode[3]);
  not not_16 (not_16_out, icode[1]);
  not not_17 (not_17_out, icode[3]);
  not not_18 (not_18_out, icode[0]);
  not not_19 (not_19_out, icode[3]);
  not not_20 (not_20_out, icode[3]);
  not not_21 (not_21_out, icode[0]);
  not not_22 (not_22_out, icode[1]);
  not not_23 (not_23_out, icode[2]);
  not not_24 (not_24_out, icode[1]);
  not not_25 (not_25_out, icode[2]);
  not not_26 (not_26_out, icode[0]);
  not not_27 (not_27_out, icode[2]);
  not not_28 (not_28_out, icode[2]);
  // AND_Gate halt has open pins: in0=not_1_out, in1=not_2_out, in2=not_3_out, in3=not_4_out, out=open
  // AND_Gate nop has open pins: in0=icode[0], in1=not_5_out, in2=not_6_out, in3=not_7_out, out=open
  // AND_Gate rr has open pins: in0=not_8_out, in1=icode[1], in2=not_9_out, in3=not_10_out, out=open
  // AND_Gate ir has open pins: in0=icode[0], in1=icode[1], in2=not_11_out, in3=not_12_out, out=open
  // AND_Gate rm has open pins: in0=not_13_out, in1=not_14_out, in2=icode[2], in3=not_15_out, out=open
  // AND_Gate mr has open pins: in0=icode[0], in1=not_16_out, in2=icode[2], in3=not_17_out, out=open
  and OPq (OPq_out, not_18_out, icode[1], icode[2], not_19_out);
  // AND_Gate jXX has open pins: in0=icode[0], in1=icode[1], in2=icode[2], in3=not_20_out, out=open
  and call (call_out, not_21_out, not_22_out, not_23_out, icode[3]);
  // AND_Gate ret has open pins: in0=icode[0], in1=not_24_out, in2=not_25_out, in3=icode[3], out=open
  and push (push_out, not_26_out, icode[1], not_27_out, icode[3]);
  // AND_Gate pop has open pins: in0=icode[0], in1=icode[1], in2=not_28_out, in3=icode[3], out=open
  and and_1 (and_1_out, OPq_out, ifun[1], ifun[0]);
  and and_2 (and_2_out, OPq_out, ifun[0]);
  and and_3 (and_3_out, OPq_out, ifun[1]);
  or or_1 (alufun[0], and_1_out, and_2_out, call_out, push_out);
  or or_2 (alufun[1], and_1_out, and_3_out);

  // Notes on the sheet:
  //   Change alufun into 0, 1, 2, or 3. 0 meaning add, 1, subtract, and 2 and 3 just go with OPq
endmodule

module SetCC (
  input  [3:0] icode,
  output set
);

  wire not_1_out, not_2_out;

  not not_1 (not_1_out, icode[0]);
  not not_2 (not_2_out, icode[3]);
  and and_1 (set, not_1_out, icode[1], icode[2], not_2_out);
endmodule

module CC (
  input  [2:0] ZSO,
  input  setcc,
  input  Clk,
  output [2:0] CCc
);

  wire decoder_1_out0, decoder_1_out1, decoder_1_out2, decoder_1_out3, decoder_1_out4, decoder_1_out5,
       decoder_1_out6, decoder_1_out7, decoder_1_out8, decoder_1_out9, decoder_1_out10, decoder_1_out11,
       decoder_1_out12, decoder_1_out13, decoder_1_out14;
  wire [3:0] counter_1_q;

  Decoder #(.enable("false"), .select(4)) decoder_1 (
    .out0(decoder_1_out0), .out1(decoder_1_out1), .out2(decoder_1_out2), .out3(decoder_1_out3),
    .out4(decoder_1_out4), .out5(decoder_1_out5), .out6(decoder_1_out6), .out7(decoder_1_out7),
    .out8(decoder_1_out8), .out9(decoder_1_out9), .out10(decoder_1_out10), .out11(decoder_1_out11),
    .out12(decoder_1_out12), .out13(decoder_1_out13), .out14(decoder_1_out14), .sel(counter_1_q));  // open: out15
  Counter #(.max('hd), .width(4)) counter_1 (.Q(counter_1_q), .clk(Clk));  // open: load, D, count, carry, up, clr
  Register #(.width(3)) register_1 (.D(ZSO), .en(setcc), .clk(decoder_1_out12), .Q(CCc));  // open: clr
endmodule

module Cond (
  input  [3:0] ifun,
  input  [2:0] CC,
  output Cnd
);

  wire and_1_out, and_2_out, and_3_out, and_4_out, and_5_out, and_6_out, je_out, jg_out, jge_out, jl_out,
       jle_out, jmp_out, jne_out, not_1_out, not_2_out, not_3_out, not_4_out, not_5_out, not_6_out,
       not_7_out, not_8_out, not_9_out, not_10_out, not_11_out, not_12_out, not_13_out, not_14_out,
       not_15_out, not_16_out, not_17_out, not_18_out, not_19_out, not_20_out, not_21_out, not_22_out,
       or_1_out, xor_1_out;

  not not_1 (not_1_out, ifun[0]);
  not not_2 (not_2_out, ifun[1]);
  not not_3 (not_3_out, ifun[2]);
  not not_4 (not_4_out, ifun[3]);
  not not_5 (not_5_out, ifun[1]);
  not not_6 (not_6_out, ifun[2]);
  not not_7 (not_7_out, ifun[3]);
  not not_8 (not_8_out, ifun[0]);
  not not_9 (not_9_out, ifun[2]);
  not not_10 (not_10_out, ifun[3]);
  not not_11 (not_11_out, ifun[2]);
  not not_12 (not_12_out, ifun[3]);
  not not_13 (not_13_out, ifun[0]);
  not not_14 (not_14_out, ifun[1]);
  not not_15 (not_15_out, ifun[3]);
  not not_16 (not_16_out, ifun[1]);
  not not_17 (not_17_out, ifun[3]);
  not not_18 (not_18_out, ifun[0]);
  not not_19 (not_19_out, ifun[3]);
  and jmp (jmp_out, not_1_out, not_2_out, not_3_out, not_4_out);
  and jle (jle_out, ifun[0], not_5_out, not_6_out, not_7_out);
  and jl (jl_out, not_8_out, ifun[1], not_9_out, not_10_out);
  and je (je_out, ifun[0], ifun[1], not_11_out, not_12_out);
  and jne (jne_out, not_13_out, not_14_out, ifun[2], not_15_out);
  and jge (jge_out, ifun[0], not_16_out, ifun[2], not_17_out);
  and jg (jg_out, not_18_out, ifun[1], ifun[2], not_19_out);
  and and_1 (and_1_out, je_out, CC[2]);
  and and_2 (and_2_out, jne_out, not_20_out);
  not not_20 (not_20_out, CC[2]);
  not not_21 (not_21_out, CC[2]);
  not not_22 (not_22_out, xor_1_out);
  xor xor_1 (xor_1_out, CC[1], CC[0]);
  or or_1 (or_1_out, CC[2], xor_1_out);
  and and_3 (and_3_out, jl_out, xor_1_out);
  and and_4 (and_4_out, jge_out, not_22_out);
  and and_5 (and_5_out, jg_out, not_21_out, not_22_out);
  and and_6 (and_6_out, jle_out, or_1_out);
  or or_2 (Cnd, jmp_out, and_6_out, and_3_out, and_1_out, and_2_out, and_4_out, and_5_out);

  // Notes on the sheet:
  //   this doesnt need icode since we assume it is 7
endmodule

module Data_Memory (
  input  Read,
  input  Write,
  input  [63:0] Addr,
  input  [63:0] Data,
  input  Clk,
  output [63:0] valM
);

  wire decoder_1_out0, decoder_1_out1, decoder_1_out2, decoder_1_out3, decoder_1_out4, decoder_1_out5,
       decoder_1_out6, decoder_1_out7, decoder_1_out8, decoder_1_out9, decoder_1_out10, decoder_1_out11,
       decoder_1_out12, decoder_1_out13, decoder_1_out14;
  wire [3:0] counter_1_q;
  wire [63:0] ram_1_dout;

  Decoder #(.enable("false"), .select(4)) decoder_1 (
    .out0(decoder_1_out0), .out1(decoder_1_out1), .out2(decoder_1_out2), .out3(decoder_1_out3),
    .out4(decoder_1_out4), .out5(decoder_1_out5), .out6(decoder_1_out6), .out7(decoder_1_out7),
    .out8(decoder_1_out8), .out9(decoder_1_out9), .out10(decoder_1_out10), .out11(decoder_1_out11),
    .out12(decoder_1_out12), .out13(decoder_1_out13), .out14(decoder_1_out14), .sel(counter_1_q));  // open: out15
  Counter #(.max('hd), .width(4)) counter_1 (.Q(counter_1_q), .clk(Clk));  // open: load, D, count, carry, up, clr
  RAM #(.addrWidth(12), .dataWidth(64)) ram_1 (
    .addr(Addr[11:0]), .we(Write), .oe(Read), .clk(decoder_1_out12), .din(Data), .dout(ram_1_dout));
  Multiplexer #(.width(64)) multiplexer_1 (.in0({64{1'b0}}), .in1(ram_1_dout), .out(valM), .sel(Read));
endmodule

module MemRead (
  input  [3:0] icode,
  output Read
);

  wire mr_out, not_1_out, not_2_out, not_3_out, not_4_out, not_5_out, not_6_out, not_7_out, not_8_out,
       not_9_out, not_10_out, not_11_out, not_12_out, not_13_out, not_14_out, not_15_out, not_16_out,
       not_17_out, not_18_out, not_19_out, not_20_out, not_21_out, not_22_out, not_23_out, not_24_out,
       not_25_out, not_26_out, not_27_out, not_28_out, pop_out, ret_out;

  not not_1 (not_1_out, icode[0]);
  not not_2 (not_2_out, icode[1]);
  not not_3 (not_3_out, icode[2]);
  not not_4 (not_4_out, icode[3]);
  not not_5 (not_5_out, icode[1]);
  not not_6 (not_6_out, icode[2]);
  not not_7 (not_7_out, icode[3]);
  not not_8 (not_8_out, icode[0]);
  not not_9 (not_9_out, icode[2]);
  not not_10 (not_10_out, icode[3]);
  not not_11 (not_11_out, icode[2]);
  not not_12 (not_12_out, icode[3]);
  not not_13 (not_13_out, icode[0]);
  not not_14 (not_14_out, icode[1]);
  not not_15 (not_15_out, icode[3]);
  not not_16 (not_16_out, icode[1]);
  not not_17 (not_17_out, icode[3]);
  not not_18 (not_18_out, icode[0]);
  not not_19 (not_19_out, icode[3]);
  not not_20 (not_20_out, icode[3]);
  not not_21 (not_21_out, icode[0]);
  not not_22 (not_22_out, icode[1]);
  not not_23 (not_23_out, icode[2]);
  not not_24 (not_24_out, icode[1]);
  not not_25 (not_25_out, icode[2]);
  not not_26 (not_26_out, icode[0]);
  not not_27 (not_27_out, icode[2]);
  not not_28 (not_28_out, icode[2]);
  // AND_Gate halt has open pins: in0=not_1_out, in1=not_2_out, in2=not_3_out, in3=not_4_out, out=open
  // AND_Gate nop has open pins: in0=icode[0], in1=not_5_out, in2=not_6_out, in3=not_7_out, out=open
  // AND_Gate rr has open pins: in0=not_8_out, in1=icode[1], in2=not_9_out, in3=not_10_out, out=open
  // AND_Gate ir has open pins: in0=icode[0], in1=icode[1], in2=not_11_out, in3=not_12_out, out=open
  // AND_Gate rm has open pins: in0=not_13_out, in1=not_14_out, in2=icode[2], in3=not_15_out, out=open
  and mr (mr_out, icode[0], not_16_out, icode[2], not_17_out);
  // AND_Gate OPq has open pins: in0=not_18_out, in1=icode[1], in2=icode[2], in3=not_19_out, out=open
  // AND_Gate jXX has open pins: in0=icode[0], in1=icode[1], in2=icode[2], in3=not_20_out, out=open
  // AND_Gate call has open pins: in0=not_21_out, in1=not_22_out, in2=not_23_out, in3=icode[3], out=open
  and ret (ret_out, icode[0], not_24_out, not_25_out, icode[3]);
  // AND_Gate push has open pins: in0=not_26_out, in1=icode[1], in2=not_27_out, in3=icode[3], out=open
  and pop (pop_out, icode[0], icode[1], not_28_out, icode[3]);
  or or_1 (Read, mr_out, ret_out, pop_out);
endmodule

module MemWrite (
  input  [3:0] icode,
  output Write
);

  wire call_out, not_1_out, not_2_out, not_3_out, not_4_out, not_5_out, not_6_out, not_7_out, not_8_out,
       not_9_out, not_10_out, not_11_out, not_12_out, not_13_out, not_14_out, not_15_out, not_16_out,
       not_17_out, not_18_out, not_19_out, not_20_out, not_21_out, not_22_out, not_23_out, not_24_out,
       not_25_out, not_26_out, not_27_out, not_28_out, push_out, rm_out;

  not not_1 (not_1_out, icode[0]);
  not not_2 (not_2_out, icode[1]);
  // AND_Gate halt has open pins: in0=not_1_out, in1=not_2_out, in2=not_3_out, in3=not_4_out, out=open
  not not_3 (not_3_out, icode[2]);
  not not_4 (not_4_out, icode[3]);
  not not_5 (not_5_out, icode[1]);
  // AND_Gate nop has open pins: in0=icode[0], in1=not_5_out, in2=not_6_out, in3=not_7_out, out=open
  not not_6 (not_6_out, icode[2]);
  not not_7 (not_7_out, icode[3]);
  not not_8 (not_8_out, icode[0]);
  // AND_Gate rr has open pins: in0=not_8_out, in1=icode[1], in2=not_9_out, in3=not_10_out, out=open
  not not_9 (not_9_out, icode[2]);
  not not_10 (not_10_out, icode[3]);
  // AND_Gate ir has open pins: in0=icode[0], in1=icode[1], in2=not_11_out, in3=not_12_out, out=open
  not not_11 (not_11_out, icode[2]);
  not not_12 (not_12_out, icode[3]);
  not not_13 (not_13_out, icode[0]);
  not not_14 (not_14_out, icode[1]);
  and rm (rm_out, not_13_out, not_14_out, icode[2], not_15_out);
  not not_15 (not_15_out, icode[3]);
  not not_16 (not_16_out, icode[1]);
  // AND_Gate mr has open pins: in0=icode[0], in1=not_16_out, in2=icode[2], in3=not_17_out, out=open
  not not_17 (not_17_out, icode[3]);
  not not_18 (not_18_out, icode[0]);
  // AND_Gate OPq has open pins: in0=not_18_out, in1=icode[1], in2=icode[2], in3=not_19_out, out=open
  not not_19 (not_19_out, icode[3]);
  // AND_Gate jXX has open pins: in0=icode[0], in1=icode[1], in2=icode[2], in3=not_20_out, out=open
  not not_20 (not_20_out, icode[3]);
  not not_21 (not_21_out, icode[0]);
  not not_22 (not_22_out, icode[1]);
  and call (call_out, not_21_out, not_22_out, not_23_out, icode[3]);
  not not_23 (not_23_out, icode[2]);
  not not_24 (not_24_out, icode[1]);
  // AND_Gate ret has open pins: in0=icode[0], in1=not_24_out, in2=not_25_out, in3=icode[3], out=open
  not not_25 (not_25_out, icode[2]);
  not not_26 (not_26_out, icode[0]);
  and push (push_out, not_26_out, icode[1], not_27_out, icode[3]);
  not not_27 (not_27_out, icode[2]);
  // AND_Gate pop has open pins: in0=icode[0], in1=icode[1], in2=not_28_out, in3=icode[3], out=open
  not not_28 (not_28_out, icode[2]);
  or or_1 (Write, rm_out, call_out, push_out);
endmodule

module MemAddress (
  input  [63:0] valA,
  input  [3:0] icode,
  input  [63:0] valE,
  output [63:0] Addr
);

  wire call_out, mr_out, not_1_out, not_2_out, not_3_out, not_4_out, not_5_out, not_6_out, not_7_out,
       not_8_out, not_9_out, not_10_out, not_11_out, not_12_out, not_13_out, not_14_out, not_15_out,
       not_16_out, not_17_out, not_18_out, not_19_out, not_20_out, not_21_out, not_22_out, not_23_out,
       not_24_out, not_25_out, not_26_out, not_27_out, not_28_out, pop_out, push_out, ret_out, rm_out;
  wire [1:0] or_2_out;

  not not_1 (not_1_out, icode[0]);
  not not_2 (not_2_out, icode[1]);
  not not_3 (not_3_out, icode[2]);
  not not_4 (not_4_out, icode[3]);
  not not_5 (not_5_out, icode[1]);
  not not_6 (not_6_out, icode[2]);
  not not_7 (not_7_out, icode[3]);
  not not_8 (not_8_out, icode[0]);
  not not_9 (not_9_out, icode[2]);
  not not_10 (not_10_out, icode[3]);
  not not_11 (not_11_out, icode[2]);
  not not_12 (not_12_out, icode[3]);
  not not_13 (not_13_out, icode[0]);
  not not_14 (not_14_out, icode[1]);
  not not_15 (not_15_out, icode[3]);
  not not_16 (not_16_out, icode[1]);
  not not_17 (not_17_out, icode[3]);
  not not_18 (not_18_out, icode[0]);
  not not_19 (not_19_out, icode[3]);
  not not_20 (not_20_out, icode[3]);
  not not_21 (not_21_out, icode[0]);
  not not_22 (not_22_out, icode[1]);
  not not_23 (not_23_out, icode[2]);
  not not_24 (not_24_out, icode[1]);
  not not_25 (not_25_out, icode[2]);
  not not_26 (not_26_out, icode[0]);
  not not_27 (not_27_out, icode[2]);
  not not_28 (not_28_out, icode[2]);
  // AND_Gate halt has open pins: in0=not_1_out, in1=not_2_out, in2=not_3_out, in3=not_4_out, out=open
  // AND_Gate nop has open pins: in0=icode[0], in1=not_5_out, in2=not_6_out, in3=not_7_out, out=open
  // AND_Gate rr has open pins: in0=not_8_out, in1=icode[1], in2=not_9_out, in3=not_10_out, out=open
  // AND_Gate ir has open pins: in0=icode[0], in1=icode[1], in2=not_11_out, in3=not_12_out, out=open
  and rm (rm_out, not_13_out, not_14_out, icode[2], not_15_out);
  and mr (mr_out, icode[0], not_16_out, icode[2], not_17_out);
  // AND_Gate OPq has open pins: in0=not_18_out, in1=icode[1], in2=icode[2], in3=not_19_out, out=open
  // AND_Gate jXX has open pins: in0=icode[0], in1=icode[1], in2=icode[2], in3=not_20_out, out=open
  and call (call_out, not_21_out, not_22_out, not_23_out, icode[3]);
  and ret (ret_out, icode[0], not_24_out, not_25_out, icode[3]);
  and push (push_out, not_26_out, icode[1], not_27_out, icode[3]);
  and pop (pop_out, icode[0], icode[1], not_28_out, icode[3]);
  or or_1 (or_2_out[1], rm_out, mr_out, call_out, push_out);
  or or_2 (or_2_out[0], ret_out, pop_out);
  Multiplexer #(.select(2), .width(64)) multiplexer_1 (
    .in1(valA), .in2(valE), .out(Addr), .sel(or_2_out));  // open: in0, in3
endmodule

module MemData (
  input  [63:0] valA,
  input  [3:0] icode,
  input  [63:0] valP,
  output [63:0] Data
);

  wire not_1_out, not_2_out, not_3_out, not_4_out, not_5_out, not_6_out, not_7_out, not_8_out, not_9_out,
       not_10_out, not_11_out, not_12_out, not_13_out, not_14_out, not_15_out, not_16_out, not_17_out,
       not_18_out, not_19_out, not_20_out, not_21_out, not_22_out, not_23_out, not_24_out, not_25_out,
       not_26_out, not_27_out, not_28_out, push_out, rm_out;
  wire [1:0] or_1_out;

  not not_1 (not_1_out, icode[0]);
  not not_2 (not_2_out, icode[1]);
  not not_3 (not_3_out, icode[2]);
  not not_4 (not_4_out, icode[3]);
  not not_5 (not_5_out, icode[1]);
  not not_6 (not_6_out, icode[2]);
  not not_7 (not_7_out, icode[3]);
  not not_8 (not_8_out, icode[0]);
  not not_9 (not_9_out, icode[2]);
  not not_10 (not_10_out, icode[3]);
  not not_11 (not_11_out, icode[2]);
  not not_12 (not_12_out, icode[3]);
  not not_13 (not_13_out, icode[0]);
  not not_14 (not_14_out, icode[1]);
  not not_15 (not_15_out, icode[3]);
  not not_16 (not_16_out, icode[1]);
  not not_17 (not_17_out, icode[3]);
  not not_18 (not_18_out, icode[0]);
  not not_19 (not_19_out, icode[3]);
  not not_20 (not_20_out, icode[3]);
  not not_21 (not_21_out, icode[0]);
  not not_22 (not_22_out, icode[1]);
  not not_23 (not_23_out, icode[2]);
  not not_24 (not_24_out, icode[1]);
  not not_25 (not_25_out, icode[2]);
  not not_26 (not_26_out, icode[0]);
  not not_27 (not_27_out, icode[2]);
  not not_28 (not_28_out, icode[2]);
  // AND_Gate halt has open pins: in0=not_1_out, in1=not_2_out, in2=not_3_out, in3=not_4_out, out=open
  // AND_Gate nop has open pins: in0=icode[0], in1=not_5_out, in2=not_6_out, in3=not_7_out, out=open
  // AND_Gate rr has open pins: in0=not_8_out, in1=icode[1], in2=not_9_out, in3=not_10_out, out=open
  // AND_Gate ir has open pins: in0=icode[0], in1=icode[1], in2=not_11_out, in3=not_12_out, out=open
  and rm (rm_out, not_13_out, not_14_out, icode[2], not_15_out);
  // AND_Gate mr has open pins: in0=icode[0], in1=not_16_out, in2=icode[2], in3=not_17_out, out=open
  // AND_Gate OPq has open pins: in0=not_18_out, in1=icode[1], in2=icode[2], in3=not_19_out, out=open
  // AND_Gate jXX has open pins: in0=icode[0], in1=icode[1], in2=icode[2], in3=not_20_out, out=open
  and call (or_1_out[1], not_21_out, not_22_out, not_23_out, icode[3]);
  // AND_Gate ret has open pins: in0=icode[0], in1=not_24_out, in2=not_25_out, in3=icode[3], out=open
  and push (push_out, not_26_out, icode[1], not_27_out, icode[3]);
  // AND_Gate pop has open pins: in0=icode[0], in1=icode[1], in2=not_28_out, in3=icode[3], out=open
  or or_1 (or_1_out[0], rm_out, push_out);
  Multiplexer #(.select(2), .width(64)) multiplexer_1 (
    .in1(valA), .in2(valP), .out(Data), .sel(or_1_out));  // open: in0, in3
endmodule

module New_PC (
  input  [3:0] icode,
  input  Cnd,
  input  [63:0] valP,
  input  [63:0] valC,
  input  [63:0] valM,
  input  Clk,
  input  [63:0] PC,
  output [63:0] NewPC
);

  wire and_1_out, and_2_out, call_out, decoder_1_out0, decoder_1_out1, decoder_1_out2, decoder_1_out3,
       decoder_1_out4, decoder_1_out5, decoder_1_out6, decoder_1_out7, decoder_1_out8, decoder_1_out9,
       decoder_1_out10, decoder_1_out11, decoder_1_out12, decoder_1_out13, decoder_1_out14, decoder_1_out15,
       halt_out, ir_out, jXX_out, mr_out, nop_out, not_1_out, not_2_out, not_3_out, not_4_out, not_5_out,
       not_6_out, not_7_out, not_8_out, not_9_out, not_10_out, not_11_out, not_12_out, not_13_out,
       not_14_out, not_15_out, not_16_out, not_17_out, not_18_out, not_19_out, not_20_out, not_21_out,
       not_22_out, not_23_out, not_24_out, not_25_out, not_26_out, not_27_out, not_28_out, not_29_out,
       OPq_out, pop_out, push_out, ret_out, rm_out, rr_out;
  wire [1:0] or_1_out;
  wire [3:0] counter_1_q;
  wire [63:0] controlled_buffer_1_out, multiplexer_1_out;

  assign controlled_buffer_1_out = halt_out ? PC : 64'bz;  // Controlled_Buffer controlled_buffer_1
  not not_1 (not_1_out, icode[0]);
  not not_2 (not_2_out, icode[1]);
  not not_3 (not_3_out, icode[2]);
  not not_4 (not_4_out, icode[3]);
  not not_5 (not_5_out, icode[1]);
  not not_6 (not_6_out, icode[2]);
  not not_7 (not_7_out, icode[3]);
  not not_8 (not_8_out, icode[0]);
  not not_9 (not_9_out, icode[2]);
  not not_10 (not_10_out, icode[3]);
  not not_11 (not_11_out, icode[2]);
  not not_12 (not_12_out, icode[3]);
  not not_13 (not_13_out, icode[0]);
  not not_14 (not_14_out, icode[1]);
  not not_15 (not_15_out, icode[3]);
  not not_16 (not_16_out, icode[1]);
  not not_17 (not_17_out, icode[3]);
  not not_18 (not_18_out, icode[0]);
  not not_19 (not_19_out, icode[3]);
  not not_20 (not_20_out, icode[3]);
  not not_21 (not_21_out, icode[0]);
  not not_22 (not_22_out, icode[1]);
  not not_23 (not_23_out, icode[2]);
  not not_24 (not_24_out, icode[1]);
  not not_25 (not_25_out, icode[2]);
  not not_26 (not_26_out, icode[0]);
  not not_27 (not_27_out, icode[2]);
  not not_28 (not_28_out, icode[2]);
  and halt (halt_out, not_1_out, not_2_out, not_3_out, not_4_out);
  and nop (nop_out, icode[0], not_5_out, not_6_out, not_7_out);
  and rr (rr_out, not_8_out, icode[1], not_9_out, not_10_out);
  and ir (ir_out, icode[0], icode[1], not_11_out, not_12_out);
  and rm (rm_out, not_13_out, not_14_out, icode[2], not_15_out);
  and mr (mr_out, icode[0], not_16_out, icode[2], not_17_out);
  and OPq (OPq_out, not_18_out, icode[1], icode[2], not_19_out);
  and jXX (jXX_out, icode[0], icode[1], icode[2], not_20_out);
  and call (call_out, not_21_out, not_22_out, not_23_out, icode[3]);
  and ret (ret_out, icode[0], not_24_out, not_25_out, icode[3]);
  and push (push_out, not_26_out, icode[1], not_27_out, icode[3]);
  and pop (pop_out, icode[0], icode[1], not_28_out, icode[3]);
  and and_1 (and_1_out, jXX_out, Cnd);
  and and_2 (and_2_out, jXX_out, not_29_out);
  not not_29 (not_29_out, Cnd);
  or or_1 (or_1_out[0], mr_out, nop_out, rr_out, ir_out, rm_out, OPq_out, push_out, pop_out, and_2_out, ret_out);
  or or_2 (or_1_out[1], call_out, ret_out, and_1_out);
  Multiplexer #(.select(2), .width(64)) multiplexer_1 (
    .in0(controlled_buffer_1_out), .in1(valP), .in2(valC), .in3(valM), .out(multiplexer_1_out), .sel(or_1_out));
  Decoder #(.enable("false"), .select(4)) decoder_1 (
    .out0(decoder_1_out0), .out1(decoder_1_out1), .out2(decoder_1_out2), .out3(decoder_1_out3),
    .out4(decoder_1_out4), .out5(decoder_1_out5), .out6(decoder_1_out6), .out7(decoder_1_out7),
    .out8(decoder_1_out8), .out9(decoder_1_out9), .out10(decoder_1_out10), .out11(decoder_1_out11),
    .out12(decoder_1_out12), .out13(decoder_1_out13), .out14(decoder_1_out14), .out15(decoder_1_out15),
    .sel(counter_1_q));
  Counter #(.max('hd), .width(4)) counter_1 (.Q(counter_1_q), .clk(Clk));  // open: load, D, count, carry, up, clr
  Register #(.width(64)) register_1 (.D(multiplexer_1_out), .en(decoder_1_out13), .clk(Clk), .Q(NewPC));  // open: clr
endmodule
